# Fritzing sketch 스텝 (saved by Fritzing 1.0.1rc)
breadboards: 1

parts:
  Driver1 = 28BYJ-48 Driver Module [part_number=ULN2003 package=THT]
  SM1 = 28BYJ-48 Stepper Motor [part_number=28BYJ-48]
  Arduino = Arduino Uno (Rev3)
  S1 = Pushbutton [package="[THT]"]
  S2 = Pushbutton [package="[THT]"]
  R1 = Resistor [tolerance=±5% power=0.25W resistance=220 package=THT]
  R2 = Resistor [tolerance=±5% power=0.25W resistance=220 package=THT]

nets:
  N1: Driver1.IN1, Arduino.D11_PWM/MOSI
  N2: Driver1.IN2, Arduino.D10_PWM/SS
  N3: Driver1.IN3, Arduino.D9_PWM
  N4: Driver1.IN4, Arduino.D8
  GND: Driver1.GND, Arduino.GND, R1.Pin_1, R2.Pin_1
  N5: Driver1.Vmotor, Arduino.5V, S1.Pin_1, S1.Pin_2, S2.Pin_1, S2.Pin_2
  N6: Driver1.blue-pin, SM1.blue-pin
  N7: Driver1.pink-pin, SM1.pink-pin
  N8: Driver1.yellow-pin, SM1.yellow-pin
  N9: Driver1.orange-pin, SM1.orange-pin
  N10: Driver1.red-pin, SM1.red-pin
  N11: Arduino.D4, S1.Pin_3, S1.Pin_4, R1.Pin_0
  N12: Arduino.D5_PWM, S2.Pin_3, S2.Pin_4, R2.Pin_0

custom parts:
  28BYJ-48 Driver Module: Generic male header
  28BYJ-48 Stepper Motor: Unipolar Stepper Motor 28BYJ-48 Top coil - pink & orange Bottom coil - blue & yellow Common rail - red Connector pins: blue - pink - yellow - orange - red
